# Fritzing sketch Analog_16_Inputs (saved by Fritzing 0.4.3b)
breadboards: 2

parts:
  Beat707_SV2_Header = female pin header, 4 pins [form="♀ (female)"]
  SV2(Bottom) = female pin header, 4 pins [form="♀ (female)"]  # not connected
  SV3 = female pin header, 4 pins [form="♀ (female)"]  # not connected
  SV3(RIGHT) = female pin header, 4 pins [form="♀ (female)"]
  SV1(Right) = female pin header, 4 pins [form="♀ (female)"]
  SV1 = female pin header, 4 pins [form="♀ (female)"]
  U1 = 74HC595 [package="DIP16 [THT]"]
  C4051_Multiplexer = IC, DIP package, 16 pins [chip_label=IC spacing=300mil]
  R1 = Rotary Potentiometer (Small)
  R2 = Rotary Potentiometer (Small)
  R3 = Rotary Potentiometer (Small)
  R4 = Rotary Potentiometer (Small)
  R5 = Rotary Potentiometer (Small)
  R6 = Rotary Potentiometer (Small)
  R7 = Rotary Potentiometer (Small)
  R8 = Rotary Potentiometer (Small)
  Next_Multiplexer_Enable = female pin header, 1 pin [form="♀ (female)"]
  Next_74HC595_(Pin_14) = female pin header, 1 pin [form="♀ (female)"]

nets:
  N1: Beat707_SV2_Header.pin1, C4051_Multiplexer.pin3
  N2: SV3(RIGHT).pin1, U1.GND, U1.OE, C4051_Multiplexer.pin7, C4051_Multiplexer.pin8
  N3: SV3(RIGHT).pin4, U1.ST_CP
  N4: SV1(Right).pin2, U1.MR
  N5: SV1(Right).pin4, U1.VCC, C4051_Multiplexer.pin16
  N6: SV1.pin1, U1.DS
  N7: SV1.pin2, U1.SH_CP
  N8: U1.Q3, Next_Multiplexer_Enable.pin1
  N9: U1.Q4, C4051_Multiplexer.pin6
  N10: U1.Q5, C4051_Multiplexer.pin9
  N11: U1.Q6, C4051_Multiplexer.pin10
  N12: U1.Q7, C4051_Multiplexer.pin11
  N13: U1.Q7', Next_74HC595_(Pin_14).pin1
  N14: C4051_Multiplexer.pin1, R5.wiper
  N15: C4051_Multiplexer.pin2, R7.wiper
  N16: C4051_Multiplexer.pin4, R8.wiper
  N17: C4051_Multiplexer.pin5, R6.wiper
  N18: C4051_Multiplexer.pin12, R4.wiper
  N19: C4051_Multiplexer.pin13, R1.wiper
  N20: C4051_Multiplexer.pin14, R2.wiper
  N21: C4051_Multiplexer.pin15, R3.wiper

notes:
  white wire = Enable
  Duplicate all connections for the next 8 Pots but instead of the white wire use the blue (Next Enable) wire
